// Logisim project main.circ as structural Verilog: 15 circuits, main circuit main
module main (
  input  E,
  input  CIN,
  input  [3:0] INPR,
  output [2:0] out_4
);

  wire and_1_out, clock_1_out, maincontrol_1_dr_ld, maincontrol_1_e__clr, maincontrol_1_hlt,
       maincontrol_1_ir_bus, maincontrol_1_ir_ld, maincontrol_1_outr__ld;
  wire [1:0] maincontrol_1_m_bus;
  wire [2:0] maincontrol_1_ar_ld, maincontrol_1_pc_ld;
  wire [3:0] AC_output, AR_output, DR_output, ir_1_output, ir_1_output_2, maincontrol_1_ac_inc,
       n4_bitlik_alu_1_output_ac, outr_output, PC_output;
  wire [6:0] maincontrol_1_alu;
  wire [7:0] controlled_buffer_1_out, ram_1_data;

  Clock clock_1 (.out(clock_1_out));
  MainControl maincontrol_1 (
    .IR__4_7(ir_1_output_2), .CLK(and_1_out), .HLT(maincontrol_1_hlt), .E__CLR(maincontrol_1_e__clr),
    .M_BUS(maincontrol_1_m_bus[0]), .M_LD(maincontrol_1_m_bus[1]), .AR_LD(maincontrol_1_ar_ld[0]),
    .AR_INC(maincontrol_1_ar_ld[1]), .AR_BUS(maincontrol_1_ar_ld[2]), .pc_ld(maincontrol_1_pc_ld[0]),
    .\pc_ınc (maincontrol_1_pc_ld[1]), .pc_bus(maincontrol_1_pc_ld[2]), .DR_LD(maincontrol_1_dr_ld),
    .AC_INC(maincontrol_1_ac_inc[0]), .AC__LD(maincontrol_1_ac_inc[1]), .AC__clear(maincontrol_1_ac_inc[2]),
    .AC__BUS(maincontrol_1_ac_inc[3]), .OUTR__LD(maincontrol_1_outr__ld), .IR_BUS(maincontrol_1_ir_bus),
    .ALU(maincontrol_1_alu), .IR_LD(maincontrol_1_ir_ld));
  and and_1 (and_1_out, ~maincontrol_1_hlt, clock_1_out);  // AND_Gate
  _4_Bitlik_ALU u_4_bitlik_alu_1 (
    .AC(AC_output), .DR(DR_output), .INPR(INPR), .AND(maincontrol_1_alu[0]), .ADD(maincontrol_1_alu[1]),
    .CMA(maincontrol_1_alu[2]), .LD_DR(maincontrol_1_alu[3]), .LD_INPR(maincontrol_1_alu[4]),
    .CIR(maincontrol_1_alu[5]), .CIL(maincontrol_1_alu[6]), .cin(CIN), .E_AC_0(E),
    .E_AC_3(maincontrol_1_e__clr), .output_AC(n4_bitlik_alu_1_output_ac));  // open: cout
  RAM #(.addrWidth(4), .bus("separate")) ram_1 (
    .addr(AR_output), .din(controlled_buffer_1_out), .data(ram_1_data), .str(maincontrol_1_m_bus[1]),
    .clk(and_1_out));  // open: sel, ld, clr
  // Probe on AR_output
  _4_Bit_Kaydedici AR (
    .in_3(controlled_buffer_1_out[3:0]), .CLK(and_1_out), .INC(maincontrol_1_ar_ld[1]),
    .LD(maincontrol_1_ar_ld[0]), .OUTPUT(AR_output));  // open: CLR
  // Probe on PC_output
  _4_Bit_Kaydedici PC (
    .in_3(controlled_buffer_1_out[3:0]), .CLK(and_1_out), .INC(maincontrol_1_pc_ld[1]),
    .LD(maincontrol_1_pc_ld[0]), .OUTPUT(PC_output));  // open: CLR
  // Probe on DR_output
  _4_Bit_Kaydedici DR (
    .in_3(controlled_buffer_1_out[3:0]), .CLK(and_1_out), .LD(maincontrol_1_dr_ld), .OUTPUT(DR_output));  // open: INC, CLR
  // Probe on AC_output
  _4_Bit_Kaydedici AC (
    .in_3(n4_bitlik_alu_1_output_ac), .CLK(and_1_out), .INC(maincontrol_1_ac_inc[0]),
    .LD(maincontrol_1_ac_inc[3]), .CLR(maincontrol_1_ac_inc[2]), .OUTPUT(AC_output));
  // Probe on outr_output
  _4_Bit_Kaydedici outr (
    .in_3(controlled_buffer_1_out[3:0]), .CLK(and_1_out), .LD(maincontrol_1_outr__ld), .OUTPUT(outr_output));  // open: INC, CLR
  // Probe on {ir_1_output_2, ir_1_output}
  IR ir_1 (
    .\input (controlled_buffer_1_out), .CLK(and_1_out), .LD(maincontrol_1_ir_bus),
    .\output ({ir_1_output_2, ir_1_output}));
  assign controlled_buffer_1_out = maincontrol_1_m_bus[0] ? ram_1_data : 8'bz;  // Controlled_Buffer controlled_buffer_1
  assign controlled_buffer_1_out = maincontrol_1_ar_ld[2] ? {4'b0000, AR_output} : 8'bz;  // Controlled_Buffer controlled_buffer_2
  assign controlled_buffer_1_out = maincontrol_1_pc_ld[2] ? {4'b0000, PC_output} : 8'bz;  // Controlled_Buffer controlled_buffer_3
  assign controlled_buffer_1_out = maincontrol_1_ac_inc[1] ? {4'b0000, AC_output} : 8'bz;  // Controlled_Buffer controlled_buffer_4
  assign controlled_buffer_1_out = maincontrol_1_ir_ld ? {ir_1_output_2, ir_1_output} : 8'bz;  // Controlled_Buffer controlled_buffer_5
endmodule

// reg.
module _4_Bit_Kaydedici (
  input  INC,
  input  LD,
  input  [3:0] in_3,
  input  CLK,
  input  CLR,
  output [3:0] OUTPUT
);

  wire and_1_out, and_2_out, and_3_out, and_4_out, and_5_out, and_6_out, and_7_out, and_8_out, and_9_out,
       and_10_out, and_11_out, and_12_out, not_1_out, not_2_out, not_3_out, not_4_out, not_5_out, not_6_out,
       or_1_out, or_2_out, or_3_out, or_4_out, or_5_out, or_6_out, or_7_out, or_8_out;

  not not_1 (not_1_out, LD);
  and and_1 (and_1_out, INC, not_1_out);
  not not_2 (not_2_out, not_1_out);
  not not_3 (not_3_out, in_3[0]);
  not not_4 (not_4_out, in_3[1]);
  not not_5 (not_5_out, in_3[2]);
  not not_6 (not_6_out, in_3[3]);
  and and_2 (and_2_out, not_2_out, in_3[0]);
  and and_3 (and_3_out, not_2_out, not_3_out);
  and and_4 (and_4_out, not_2_out, in_3[1]);
  and and_5 (and_5_out, not_2_out, not_4_out);
  and and_6 (and_6_out, not_2_out, in_3[2]);
  and and_7 (and_7_out, not_2_out, not_5_out);
  and and_8 (and_8_out, not_2_out, in_3[3]);
  and and_9 (and_9_out, not_2_out, not_6_out);
  and and_10 (and_10_out, and_1_out, OUTPUT[0], OUTPUT[1], OUTPUT[2]);
  and and_11 (and_11_out, and_1_out, OUTPUT[0]);
  and and_12 (and_12_out, and_1_out, OUTPUT[0], OUTPUT[1]);
  or or_1 (or_1_out, and_4_out, and_11_out);
  or or_2 (or_2_out, and_11_out, and_5_out);
  or or_3 (or_3_out, and_6_out, and_12_out);
  or or_4 (or_4_out, and_12_out, and_7_out);
  or or_5 (or_5_out, and_8_out, and_10_out);
  or or_6 (or_6_out, and_10_out, and_9_out);
  or or_7 (or_7_out, and_2_out, and_1_out);
  or or_8 (or_8_out, and_3_out, and_1_out);
  J_K_Flip_Flop j_k_ff_1 (.J(or_7_out), .clk(CLK), .K(or_8_out), .Q(OUTPUT[0]), .reset(CLR));  // open: Qn, preset, en
  J_K_Flip_Flop j_k_ff_2 (.J(or_1_out), .clk(CLK), .K(or_2_out), .Q(OUTPUT[1]), .reset(CLR));  // open: Qn, preset, en
  J_K_Flip_Flop j_k_ff_3 (.J(or_3_out), .clk(CLK), .K(or_4_out), .Q(OUTPUT[2]), .reset(CLR));  // open: Qn, preset, en
  J_K_Flip_Flop j_k_ff_4 (.J(or_5_out), .clk(CLK), .K(or_6_out), .Q(OUTPUT[3]), .reset(CLR));  // open: Qn, preset, en
endmodule

module _1_Bit_ALU (
  input  INPR,
  input  DR,
  input  AC,
  input  AND,
  input  cin,
  input  ADD,
  input  CMA,
  input  LD_DR,
  input  LD_INPR,
  input  CIR,
  input  CIL,
  input  AC_i_1,
  input  AC_i_1_2,
  output cout,
  output output_AC
);

  wire add_out, adder_1_out, and_out, comp_out, Id_DR_out, Id_INPR_out, not_1_out, shl_out, shr_out;

  Adder #(.width(1)) adder_1 (.a(AC), .b(DR), .out(adder_1_out), .cin(cin), .cout(cout));
  not not_1 (not_1_out, AC);
  and u_and (and_out, AND, AC, DR);
  and u_add (add_out, ADD, adder_1_out);
  and comp (comp_out, CMA, not_1_out);
  and Id_DR (Id_DR_out, LD_DR, DR);
  and Id_INPR (Id_INPR_out, LD_INPR, INPR);
  and shr (shr_out, CIR, AC_i_1_2);
  and shl (shl_out, CIL, AC_i_1);
  or or_1 (output_AC, and_out, add_out, comp_out, Id_DR_out, Id_INPR_out, shr_out, shl_out);
endmodule

// ALU
module _4_Bitlik_ALU (
  input  cin,
  input  E_AC_0,
  input  [3:0] AC,
  input  [3:0] DR,
  input  [3:0] INPR,
  input  AND,
  input  ADD,
  input  CMA,
  input  LD_DR,
  input  LD_INPR,
  input  CIR,
  input  CIL,
  input  E_AC_3,
  output [3:0] output_AC,
  output cout
);

  wire n1_bit_alu_1_cout, n1_bit_alu_2_cout, n1_bit_alu_3_cout;

  _1_Bit_ALU u_1_bit_alu_1 (
    .AND(AND), .ADD(ADD), .CMA(CMA), .LD_DR(LD_DR), .LD_INPR(LD_INPR), .CIR(CIR), .CIL(CIL), .AC_i_1(E_AC_0),
    .AC_i_1_2(AC[1]), .INPR(INPR[0]), .DR(DR[0]), .AC(AC[0]), .cin(cin), .cout(n1_bit_alu_1_cout),
    .output_AC(output_AC[0]));
  _1_Bit_ALU u_1_bit_alu_2 (
    .AND(AND), .ADD(ADD), .CMA(CMA), .LD_DR(LD_DR), .LD_INPR(LD_INPR), .CIR(CIR), .CIL(CIL), .AC_i_1(AC[0]),
    .AC_i_1_2(AC[2]), .INPR(INPR[1]), .DR(DR[1]), .AC(AC[1]), .cin(n1_bit_alu_1_cout),
    .cout(n1_bit_alu_2_cout), .output_AC(output_AC[1]));
  _1_Bit_ALU u_1_bit_alu_3 (
    .AND(AND), .ADD(ADD), .CMA(CMA), .LD_DR(LD_DR), .LD_INPR(LD_INPR), .CIR(CIR), .CIL(CIL), .AC_i_1(AC[1]),
    .AC_i_1_2(AC[3]), .INPR(INPR[2]), .DR(DR[2]), .AC(AC[2]), .cin(n1_bit_alu_2_cout),
    .cout(n1_bit_alu_3_cout), .output_AC(output_AC[2]));
  _1_Bit_ALU u_1_bit_alu_4 (
    .AND(AND), .ADD(ADD), .CMA(CMA), .LD_DR(LD_DR), .LD_INPR(LD_INPR), .CIR(CIR), .CIL(CIL), .AC_i_1(AC[2]),
    .AC_i_1_2(E_AC_3), .INPR(INPR[3]), .DR(DR[3]), .AC(AC[3]), .cin(n1_bit_alu_3_cout), .cout(cout),
    .output_AC(output_AC[3]));
endmodule

module IR (
  input  [7:0] \input ,
  input  CLK,
  input  LD,
  output [7:0] \output 
);

  _4_Bit_Kaydedici u_4_bit_kaydedici_1 (
    .in_3(\input [3:0]), .CLK(CLK), .LD(LD), .OUTPUT(\output [3:0]));  // open: INC, CLR
  _4_Bit_Kaydedici u_4_bit_kaydedici_2 (
    .in_3(\input [7:4]), .CLK(CLK), .LD(LD), .OUTPUT(\output [7:4]));  // open: INC, CLR
endmodule

// AR
module AR_CONT (
  input  T0,
  input  T2,
  input  T3,
  input  T4,
  input  D4,
  input  D5,
  output AR_LD,
  output AR_INC,
  output AR_BUS
);

  wire and_1_out, and_2_out;

  and and_1 (and_1_out, D5, T4);
  and and_2 (and_2_out, D4, T3);
  or or_1 (AR_LD, T2, T0);
  and and_3 (AR_INC, T3, D5);
  or or_2 (AR_BUS, and_1_out, and_2_out);
endmodule

// DR
module DR_CONT (
  input  T3,
  input  D0,
  input  D1,
  input  D2,
  output DR_LOAD
);

  wire or_1_out;

  or or_1 (or_1_out, D2, D1, D0);
  and and_1 (DR_LOAD, or_1_out, T3);
endmodule

// PC
module PC_CONT (
  input  T0,
  input  T1,
  input  T2,
  input  T3,
  input  D4,
  input  D5,
  input  D6,
  output pc_ld,
  output \pc_ınc ,
  output pc_bus
);

  wire and_1_out, and_2_out, and_3_out, or_1_out;

  or or_1 (or_1_out, D6, D4);
  and and_1 (and_1_out, or_1_out, T2);
  and and_2 (and_2_out, D5, T3);
  and and_3 (and_3_out, D5, T2);
  or or_2 (pc_ld, and_1_out, and_2_out);
  or or_3 (pc_bus, and_3_out, T0);

  assign \pc_ınc  = T1;
endmodule

// AC
module AC_CONT (
  input  T3,
  input  T4,
  input  D0,
  input  D1,
  input  D2,
  input  D3,
  input  D7,
  input  D9,
  input  D10,
  input  D11,
  input  D12,
  input  D13,
  input  D14,
  output AC_INC,
  output AC__BUS,
  output AC__clear,
  output AC__LD
);

  wire and_4_out, and_5_out, or_1_out, or_2_out, or_3_out;

  or or_1 (or_1_out, D14, D3);
  or or_2 (or_2_out, D12, D11, D13, D9, D7);
  or or_3 (or_3_out, D2, D1, D0);
  and and_1 (AC__clear, D7, T3);
  and and_2 (AC_INC, D10, T3);
  and and_3 (AC__BUS, or_1_out, T3);
  and and_4 (and_4_out, or_2_out, T3);
  and and_5 (and_5_out, or_3_out, T4);
  or or_4 (AC__LD, and_4_out, and_5_out);
endmodule

// IR
module IR_CONT (
  input  T1,
  input  T2,
  output IR_LD,
  output IR_BUS
);


  assign IR_BUS = T2;
  assign IR_LD = T1;
endmodule

module M_CONT (
  input  T1,
  input  T3,
  input  D0,
  input  D1,
  input  D2,
  input  D3,
  input  D5,
  input  D6,
  output M_BUS,
  output M_LD
);

  wire and_1_out, or_1_out, or_2_out;

  or or_1 (or_1_out, D6, D2, D1, D0);
  or or_2 (or_2_out, D5, D3);
  and and_1 (and_1_out, or_1_out, T3);
  and and_2 (M_LD, or_2_out, T3);
  or or_3 (M_BUS, and_1_out, T1);
endmodule

// Register Kontrol
module RegisterKontrol (
  input  T0,
  input  T1,
  input  T2,
  input  T3,
  input  T4,
  input  D0,
  input  D1,
  input  D2,
  input  D3,
  input  D4,
  input  D5,
  input  D6,
  input  D7,
  input  D8,
  input  D9,
  input  D10,
  input  D11,
  input  D12,
  input  D13,
  input  D14,
  output M_BUS,
  output M_LD,
  output AR_BUS,
  output AR_INC,
  output AR_LD,
  output pc_ld,
  output \pc_ınc ,
  output pc_bus,
  output DR_LD,
  output AC_INC,
  output AC__LD,
  output AC__clear,
  output AC__BUS,
  output OUTR__LD,
  output IR_BUS,
  output IR_LD
);

  M_CONT m_cont_1 (.T1(T1), .T3(T3), .D0(D0), .D1(D1), .D2(D2), .D3(D3), .D5(D5), .D6(D6), .M_BUS(M_BUS), .M_LD(M_LD));
  AR_CONT ar_cont_1 (
    .T0(T0), .T2(T2), .T3(T3), .T4(T4), .D4(D4), .D5(D5), .AR_LD(AR_BUS), .AR_INC(AR_INC), .AR_BUS(AR_LD));
  PC_CONT pc_cont_1 (
    .T0(T0), .T1(T1), .T2(T2), .T3(T3), .D4(D4), .D5(D5), .D6(D6), .pc_ld(pc_ld), .\pc_ınc (\pc_ınc ),
    .pc_bus(pc_bus));
  DR_CONT dr_cont_1 (.T3(T3), .D0(D2), .D1(D1), .D2(D0), .DR_LOAD(DR_LD));
  and and_1 (OUTR__LD, D14, T3);
  AC_CONT ac_cont_1 (
    .T3(T3), .T4(T4), .D0(D0), .D1(D1), .D2(D2), .D3(D3), .D7(D7), .D9(D9), .D10(D10), .D11(D11), .D12(D12),
    .D13(D13), .D14(D14), .AC_INC(AC_INC), .AC__BUS(AC__LD), .AC__clear(AC__clear), .AC__LD(AC__BUS));

  assign IR_BUS = T1;
  assign IR_LD = T2;
endmodule

// Alu Control
module AluKontrol (
  input  T3,
  input  T4,
  input  D0,
  input  D1,
  input  D2,
  input  D9,
  input  D11,
  input  D12,
  input  D13,
  output [6:0] Alu_output
);

  wire or_1_out;

  or or_1 (or_1_out, T4, T3);
  and and_1 (Alu_output[0], D12, T3);
  and and_2 (Alu_output[1], D11, T3);
  and and_3 (Alu_output[2], D13, T3);
  and and_4 (Alu_output[3], D2, or_1_out);
  and and_5 (Alu_output[4], D9, T3);
  and and_6 (Alu_output[5], D1, or_1_out);
  and and_7 (Alu_output[6], or_1_out, D0);
endmodule

module SC_CLEAR (
  input  T3,
  input  T4,
  input  D0,
  input  D1,
  input  D2,
  input  D3,
  input  D4,
  input  D5,
  input  D6,
  input  D7,
  input  D8,
  input  D9,
  input  D10,
  input  D11,
  input  D12,
  input  D13,
  input  D14,
  output CLR
);

  wire and_1_out, and_2_out, or_1_out, or_2_out;

  or or_1 (or_1_out, D5, D2, D1, D0);
  or or_2 (or_2_out, D6, D4, D3);
  and and_1 (and_1_out, or_1_out, T4);
  and and_2 (and_2_out, T3, or_2_out);
  or or_3 (CLR, and_1_out, and_2_out);
endmodule

module MainControl (
  input  [3:0] IR__4_7,
  input  CLK,
  output M_BUS,
  output M_LD,
  output AR_LD,
  output AR_INC,
  output AR_BUS,
  output pc_ld,
  output \pc_ınc ,
  output pc_bus,
  output DR_LD,
  output AC_INC,
  output AC__LD,
  output AC__clear,
  output AC__BUS,
  output OUTR__LD,
  output IR_BUS,
  output [6:0] ALU,
  output IR_LD,
  output HLT,
  output E__CLR
);

  wire d_ff_1_q, decoder_1_out15, sc_clear_1_clr;
  wire [1:0] decoder_2_out4;
  wire [2:0] counter_2_q, decoder_2_out0;
  wire [6:0] decoder_1_out0;
  wire [14:3] decoder_1_out3;

  SC_CLEAR sc_clear_1 (
    .T3(decoder_2_out4[1]), .T4(decoder_2_out4[0]), .D0(decoder_1_out0[6]), .D1(decoder_1_out0[5]),
    .D2(decoder_1_out0[4]), .D3(decoder_1_out3[3]), .D4(decoder_1_out3[4]), .D5(decoder_1_out3[5]),
    .D6(decoder_1_out3[6]), .D7(decoder_1_out3[7]), .D8(decoder_1_out3[8]), .D9(decoder_1_out0[3]),
    .D10(decoder_1_out3[10]), .D11(decoder_1_out0[2]), .D12(decoder_1_out0[1]), .D13(decoder_1_out0[0]),
    .D14(decoder_1_out3[14]), .CLR(sc_clear_1_clr));
  Counter counter_1 ();  // open: load, D, count, Q, carry, clk, clr
  Decoder #(.select(4)) decoder_1 (
    .out0(decoder_1_out0[6]), .out1(decoder_1_out0[5]), .out2(decoder_1_out0[4]), .out3(decoder_1_out3[3]),
    .out4(decoder_1_out3[4]), .out5(decoder_1_out3[5]), .out6(decoder_1_out3[6]), .out7(decoder_1_out3[7]),
    .out8(decoder_1_out3[8]), .out9(decoder_1_out0[3]), .out10(decoder_1_out3[10]),
    .out11(decoder_1_out0[2]), .out12(decoder_1_out0[1]), .out13(decoder_1_out0[0]),
    .out14(decoder_1_out3[14]), .out15(decoder_1_out15), .sel(IR__4_7));  // open: en
  Decoder #(.select(3)) decoder_2 (
    .out0(decoder_2_out0[0]), .out1(decoder_2_out0[1]), .out2(decoder_2_out0[2]), .out3(decoder_2_out4[1]),
    .out4(decoder_2_out4[0]), .sel(counter_2_q));  // open: out5, out6, out7, en
  Counter #(.width(3), .max('h7)) counter_2 (
    .Q(counter_2_q), .clk(CLK), .clr(d_ff_1_q));  // open: load, D, count, carry
  D_Flip_Flop d_ff_1 (.clk(CLK), .D(sc_clear_1_clr), .Q(d_ff_1_q));  // open: Qn, preset, en, reset
  and and_1 (HLT, decoder_1_out15, decoder_2_out4[1]);
  and and_2 (E__CLR, decoder_2_out4[1], decoder_1_out3[8]);
  AluKontrol alukontrol_1 (
    .T3(decoder_2_out4[1]), .T4(decoder_2_out4[0]), .D0(decoder_1_out0[6]), .D1(decoder_1_out0[5]),
    .D2(decoder_1_out0[4]), .D9(decoder_1_out0[3]), .D11(decoder_1_out0[2]), .D12(decoder_1_out0[1]),
    .D13(decoder_1_out0[0]), .Alu_output(ALU));
  RegisterKontrol registerkontrol_1 (
    .T0(decoder_2_out0[0]), .T1(decoder_2_out0[1]), .T2(decoder_2_out0[2]), .T3(decoder_2_out4[1]),
    .T4(decoder_2_out4[0]), .D0(decoder_1_out0[6]), .D1(decoder_1_out0[5]), .D2(decoder_1_out0[4]),
    .D3(decoder_1_out3[3]), .D4(decoder_1_out3[4]), .D5(decoder_1_out3[5]), .D6(decoder_1_out3[6]),
    .D7(decoder_1_out3[7]), .D8(decoder_1_out3[8]), .D9(decoder_1_out0[3]), .D10(decoder_1_out3[10]),
    .D11(decoder_1_out0[2]), .D12(decoder_1_out0[1]), .D13(decoder_1_out0[0]), .D14(decoder_1_out3[14]),
    .M_BUS(M_BUS), .M_LD(M_LD), .AR_BUS(AR_LD), .AR_INC(AR_INC), .AR_LD(AR_BUS), .pc_ld(pc_ld),
    .\pc_ınc (\pc_ınc ), .pc_bus(pc_bus), .DR_LD(DR_LD), .AC_INC(AC_INC), .AC__LD(AC__LD),
    .AC__clear(AC__clear), .AC__BUS(AC__BUS), .OUTR__LD(OUTR__LD), .IR_BUS(IR_BUS), .IR_LD(IR_LD));
endmodule
